// Logisim project cao.circ as structural Verilog: 24 circuits, main circuit main
module main (
);

  wire ac_controller_1_clr, ac_controller_1_inc, ac_controller_1_ld, alu_1_cout, ar_controller_1_p2,
       ar_controller_1_p3, ar_controller_1_p4, CLK_out, dr_controller_1_inc, dr_controller_1_ld,
       e_control_1_clr, e_control_1_ld, ir_controller_1_ld, pc_controller_1_inc, pc_controller_1_ld,
       sc_controller_1_p2, sc_controller_1_p4, tr_controller_1_ld;
  wire [2:0] ac_controller_1_aluout;
  wire [3:0] sc_1_tout;
  wire [21:0] AC, alu_1_out, AR, DR, IR, Mem, PC, TR, undriven;
  wire [21:16] undriven_2;

  AR ar_1 (
    .in(undriven), .LD(ar_controller_1_p2), .INC(ar_controller_1_p3), .CLR(ar_controller_1_p4),
    .CLK(CLK_out), .out(AR));
  TR tr_1 (.in(undriven), .LD(tr_controller_1_ld), .CLK(CLK_out), .out(TR));  // open: INC, CLR
  TR_Controller tr_controller_1 (.IR(IR), .LD(tr_controller_1_ld));  // open: Seq, R
  // AR_controller ar_controller_1: pin names not known; wires that end beside it: IR, ar_controller_1_p2, ar_controller_1_p3, ar_controller_1_p4
  IR ir_1 (.in(undriven), .LD(ir_controller_1_ld), .CLK(CLK_out), .out(IR));
  IR_Controller ir_controller_1 (.T(sc_1_tout), .LD(ir_controller_1_ld));  // open: R
  DR dr_1 (.in(undriven), .LD(dr_controller_1_ld), .INC(dr_controller_1_inc), .CLK(CLK_out), .out(DR));  // open: CLR
  DR_Controller dr_controller_1 (.IR(IR), .LD(dr_controller_1_ld), .INC(dr_controller_1_inc));  // open: Seq
  PC_Controller pc_controller_1 (
    .IR(IR), .INC(pc_controller_1_inc), .LD(pc_controller_1_ld));  // open: CLR, DR, DR_2, R, Seq, E, FGO, FGI
  AC ac_1 (
    .in(alu_1_out), .LD(ac_controller_1_ld), .INC(ac_controller_1_inc), .CLR(ac_controller_1_clr),
    .CLK(CLK_out), .out(AC));
  AC_Controller ac_controller_1 (
    .IR(IR), .ALUout(ac_controller_1_aluout), .LD(ac_controller_1_ld), .CLR(ac_controller_1_clr),
    .INC(ac_controller_1_inc));  // open: Seq
  RAM #(.addrWidth(22), .dataWidth(22), .bus("separate")) ram_1 (
    .addr({undriven_2, AR[15:0]}), .din(undriven), .data(Mem), .clk(CLK_out));  // open: str, sel, ld, clr
  PC pc_1 (.in(undriven), .LD(pc_controller_1_ld), .INC(pc_controller_1_inc), .CLK(CLK_out), .out(PC));
  E_Control e_control_1 (.IR(IR), .LD(e_control_1_ld), .CLR(e_control_1_clr));  // open: comp, Seq
  E e_1 (.in(alu_1_cout), .CLK(CLK_out), .LD(e_control_1_ld), .CLR(e_control_1_clr));  // open: Comp, out
  ALU alu_1 (.in(undriven), .DR(DR), .Select(ac_controller_1_aluout), .out(alu_1_out), .Cout(alu_1_cout));
  Clock CLK (.out(CLK_out));
  SC sc_1 (.CLK(CLK_out), .CLR(sc_controller_1_p4), .Tout(sc_1_tout));
  // SC_Controller sc_controller_1: pin names not known; wires that end beside it: IR, sc_controller_1_p2, sc_controller_1_p2, sc_controller_1_p4
endmodule

module AR_controller (
  input  [21:0] IR,
  input  [15:0] Seq,
  input  I0,
  input  I1,
  input  R,
  output LD,
  output INR,
  output CLR
);

  wire and_1_out, and_2_out, and_3_out, decoder_2_out0, decoder_2_out1, decoder_2_out2, decoder_2_out3,
       decoder_2_out4, decoder_2_out5, decoder_2_out6, decoder_2_out7, decoder_2_out8, decoder_2_out9,
       decoder_2_out10, decoder_2_out11, decoder_2_out12, decoder_2_out13, decoder_2_out14, decoder_2_out15,
       I2, I3, m;

  or or_1 (m, I0, I1);
  Decoder #(.select(2)) decoder_1 (.out0(I0), .out1(I1), .out2(I2), .out3(I3), .sel(IR[21:20]));  // open: en
  Decoder #(.select(4)) decoder_2 (
    .out0(decoder_2_out0), .out1(decoder_2_out1), .out2(decoder_2_out2), .out3(decoder_2_out3),
    .out4(decoder_2_out4), .out5(decoder_2_out5), .out6(decoder_2_out6), .out7(decoder_2_out7),
    .out8(decoder_2_out8), .out9(decoder_2_out9), .out10(decoder_2_out10), .out11(decoder_2_out11),
    .out12(decoder_2_out12), .out13(decoder_2_out13), .out14(decoder_2_out14), .out15(decoder_2_out15),
    .sel(IR[19:16]));  // open: en
  and and_1 (and_1_out, I1, Seq[3]);
  and and_2 (and_2_out, Seq[0], ~R);  // AND_Gate
  and and_3 (and_3_out, ~R, Seq[2]);  // AND_Gate
  and and_4 (INR, decoder_2_out5, m, Seq[4]);
  and and_5 (CLR, Seq[0], R);
  or or_2 (LD, and_1_out, and_2_out, and_3_out);
endmodule

module AR (
  input  [21:0] in,
  input  LD,
  input  INC,
  input  CLR,
  input  CLK,
  output [21:0] out
);

  wire [15:0] adder_1_out, multiplexer_1_out;

  Adder #(.width(16)) adder_1 (.a(out[15:0]), .b(16'h1), .out(adder_1_out));  // open: cin, cout
  Multiplexer #(.width(16)) multiplexer_1 (
    .in0(in[15:0]), .in1(adder_1_out), .out(multiplexer_1_out), .sel(INC));  // open: en
  Register #(.width(16)) register_1 (.D(multiplexer_1_out), .en(LD), .Q(out[15:0]), .clk(CLK), .clr(CLR));
endmodule

module DR_Controller (
  input  [21:0] IR,
  input  [15:0] Seq,
  output LD,
  output INC
);

  wire and_1_out, and_2_out, and_3_out, and_4_out, and_5_out, and_6_out, and_7_out, decoder_2_out0,
       decoder_2_out1, decoder_2_out2, decoder_2_out3, decoder_2_out4, decoder_2_out5, decoder_2_out6,
       decoder_2_out7, decoder_2_out8, decoder_2_out9, decoder_2_out10, decoder_2_out11, decoder_2_out12,
       decoder_2_out13, decoder_2_out14, decoder_2_out15, I0, I1, I2, I3, m;

  Decoder #(.select(2)) decoder_1 (.out0(I0), .out1(I1), .out2(I2), .out3(I3), .sel(IR[21:20]));  // open: en
  or or_1 (m, I0, I1);
  Decoder #(.select(4)) decoder_2 (
    .out0(decoder_2_out0), .out1(decoder_2_out1), .out2(decoder_2_out2), .out3(decoder_2_out3),
    .out4(decoder_2_out4), .out5(decoder_2_out5), .out6(decoder_2_out6), .out7(decoder_2_out7),
    .out8(decoder_2_out8), .out9(decoder_2_out9), .out10(decoder_2_out10), .out11(decoder_2_out11),
    .out12(decoder_2_out12), .out13(decoder_2_out13), .out14(decoder_2_out14), .out15(decoder_2_out15),
    .sel(IR[19:16]));  // open: en
  and and_1 (and_1_out, m, decoder_2_out0, Seq[4]);
  and and_2 (and_2_out, m, decoder_2_out1, Seq[4]);
  and and_3 (and_3_out, m, decoder_2_out2, Seq[4]);
  and and_4 (and_4_out, m, decoder_2_out6, Seq[4]);
  and and_5 (and_5_out, m, decoder_2_out7, Seq[4]);
  and and_6 (and_6_out, m, decoder_2_out8, Seq[4]);
  and and_7 (and_7_out, m, decoder_2_out9, Seq[4]);
  and and_8 (INC, m, decoder_2_out6, Seq[5]);
  or or_2 (LD, and_1_out, and_2_out, and_3_out, and_4_out, and_5_out, and_6_out, and_7_out);
endmodule

module DR (
  input  [21:0] in,
  input  LD,
  input  INC,
  input  CLR,
  input  CLK,
  output [21:0] out
);

  wire or_1_out;
  wire [21:0] adder_1_out, multiplexer_1_out;

  Adder #(.width(22)) adder_1 (.a(out), .b(22'h1), .out(adder_1_out));  // open: cin, cout
  or or_1 (or_1_out, LD, INC);
  Multiplexer #(.width(22)) multiplexer_1 (
    .in0(in), .in1(adder_1_out), .out(multiplexer_1_out), .sel(INC));  // open: en
  Register #(.width(22)) register_1 (.D(multiplexer_1_out), .en(or_1_out), .Q(out), .clk(CLK), .clr(CLR));
endmodule

module PC_Controller (
  input  [21:0] IR,
  input  E,
  input  FGO,
  input  FGI,
  input  R,
  input  [15:0] Seq,
  input  [21:0] DR,
  input  [21:0] DR_2,
  output INC,
  output LD,
  output CLR
);

  wire ac, and_4_out, and_5_out, and_6_out, and_7_out, and_8_out, and_9_out, and_10_out, and_11_out,
       and_12_out, and_13_out, and_14_out, and_15_out, and_16_out, and_17_out, and_18_out, and_19_out,
       and_20_out, and_21_out, d, decoder_2_out0, decoder_2_out1, decoder_2_out2, decoder_2_out3,
       decoder_2_out4, decoder_2_out5, decoder_2_out6, decoder_2_out7, decoder_2_out8, decoder_2_out9,
       decoder_2_out10, decoder_2_out11, decoder_2_out12, decoder_2_out13, decoder_2_out14, decoder_2_out15,
       I0, I1, I2, I3, m, p, r_t;

  and and_1 (r_t, I2, Seq[3]);
  and and_2 (p, I3, Seq[3]);
  Decoder #(.select(2)) decoder_1 (.out0(I0), .out1(I1), .out2(I2), .out3(I3), .sel(IR[21:20]));  // open: en
  or or_1 (m, I0, I1);
  Decoder #(.select(4)) decoder_2 (
    .out0(decoder_2_out0), .out1(decoder_2_out1), .out2(decoder_2_out2), .out3(decoder_2_out3),
    .out4(decoder_2_out4), .out5(decoder_2_out5), .out6(decoder_2_out6), .out7(decoder_2_out7),
    .out8(decoder_2_out8), .out9(decoder_2_out9), .out10(decoder_2_out10), .out11(decoder_2_out11),
    .out12(decoder_2_out12), .out13(decoder_2_out13), .out14(decoder_2_out14), .out15(decoder_2_out15),
    .sel(IR[19:16]));  // open: en
  or or_2 (d, DR[21], DR[20], DR[19], DR[18], DR[17], DR[16], DR[15], DR[14], DR[13], DR[12], DR[11], DR[10], DR[8], DR[7], DR[6], DR[5], DR[4], DR[3], DR[2], DR[1], DR[0], DR[9]);
  and and_3 (CLR, R, Seq[1]);
  or or_3 (ac, DR_2[21], DR_2[20], DR_2[19], DR_2[18], DR_2[17], DR_2[16], DR_2[15], DR_2[14], DR_2[13], DR_2[12], DR_2[11], DR_2[10], DR_2[8], DR_2[7], DR_2[6], DR_2[5], DR_2[4], DR_2[3], DR_2[2], DR_2[1], DR_2[0], DR_2[9]);
  and and_4 (and_4_out, ~R, Seq[1]);  // AND_Gate
  and and_5 (and_5_out, R, Seq[2]);
  and and_6 (and_6_out, m, decoder_2_out6, Seq[6]);
  and and_7 (and_7_out, r_t, decoder_2_out7);
  and and_8 (and_8_out, r_t, decoder_2_out8);
  and and_9 (and_9_out, r_t, decoder_2_out10);
  and and_10 (and_10_out, p, decoder_2_out2);
  and and_11 (and_11_out, p, decoder_2_out3);
  and and_12 (and_12_out, m, decoder_2_out4, Seq[4]);
  and and_13 (and_13_out, m, decoder_2_out5, Seq[5]);
  and and_14 (and_14_out, r_t, decoder_2_out9);
  and and_15 (and_15_out, and_10_out, FGO);
  and and_16 (and_16_out, and_11_out, FGI);
  or or_4 (LD, and_12_out, and_13_out);
  and and_17 (and_17_out, and_6_out, ~d);  // AND_Gate
  and and_18 (and_18_out, and_7_out, ~DR_2[21]);  // AND_Gate
  and and_19 (and_19_out, and_8_out, DR_2[21]);
  and and_20 (and_20_out, and_14_out, ac);
  and and_21 (and_21_out, and_9_out, ~E);  // AND_Gate
  or or_5 (INC, and_4_out, and_5_out, and_17_out, and_18_out, and_19_out, and_20_out, and_21_out, and_15_out, and_16_out);

  // Other names for the same wires on the sheet: ac21 = DR_2[21]
endmodule

module AC (
  input  [21:0] in,
  input  LD,
  input  INC,
  input  CLR,
  input  CLK,
  output [21:0] out
);

  wire or_1_out;
  wire [21:0] adder_1_out, multiplexer_1_out;

  Adder #(.width(22)) adder_1 (.a(out), .b(22'h1), .out(adder_1_out));  // open: cin, cout
  or or_1 (or_1_out, LD, INC);
  Multiplexer #(.width(22)) multiplexer_1 (
    .in0(in), .in1(adder_1_out), .out(multiplexer_1_out), .sel(INC));  // open: en
  Register #(.width(22)) register_1 (.D(multiplexer_1_out), .en(or_1_out), .Q(out), .clk(CLK), .clr(CLR));
endmodule

module AC_Controller (
  input  [21:0] IR,
  input  [15:0] Seq,
  output [2:0] ALUout,
  output LD,
  output CLR,
  output INC
);

  wire ADD_out, AND_3_out, and_4_out, CME_out, decoder_2_out0, decoder_2_out1, decoder_2_out2,
       decoder_2_out3, decoder_2_out4, decoder_2_out5, decoder_2_out6, decoder_2_out7, decoder_2_out8,
       decoder_2_out9, decoder_2_out10, decoder_2_out11, decoder_2_out12, decoder_2_out13, decoder_2_out14,
       decoder_2_out15, I0, I1, I2, I3, INC_out, LD_out, m, OR_2_out, p, r, SHL_out, SHR_out, XCHG_out,
       XOR_out;

  and and_1 (r, I2, Seq[3]);
  and and_2 (p, I3, Seq[3]);
  Decoder #(.select(2)) decoder_1 (.out0(I0), .out1(I1), .out2(I2), .out3(I3), .sel(IR[21:20]));  // open: en
  or or_1 (m, I0, I1);
  Decoder #(.select(4)) decoder_2 (
    .out0(decoder_2_out0), .out1(decoder_2_out1), .out2(decoder_2_out2), .out3(decoder_2_out3),
    .out4(decoder_2_out4), .out5(decoder_2_out5), .out6(decoder_2_out6), .out7(decoder_2_out7),
    .out8(decoder_2_out8), .out9(decoder_2_out9), .out10(decoder_2_out10), .out11(decoder_2_out11),
    .out12(decoder_2_out12), .out13(decoder_2_out13), .out14(decoder_2_out14), .out15(decoder_2_out15),
    .sel(IR[19:16]));  // open: en
  and AND_3 (AND_3_out, m, decoder_2_out0, Seq[5]);
  and ADD (ADD_out, m, decoder_2_out1, Seq[5]);
  and u_LD (LD_out, m, decoder_2_out2, Seq[5]);
  and OR_2 (OR_2_out, m, decoder_2_out7, Seq[5]);
  and XOR (XOR_out, m, decoder_2_out8, Seq[5]);
  and XCHG (XCHG_out, m, decoder_2_out9, Seq[5]);
  and u_INC (INC_out, r, decoder_2_out6);
  and CME (CME_out, r, decoder_2_out2);
  and SHR (SHR_out, r, decoder_2_out4);
  and SHL (SHL_out, r, decoder_2_out5);
  and and_4 (and_4_out, p, decoder_2_out0);
  and and_5 (CLR, r, decoder_2_out0);
  and and_6 (INC, r, decoder_2_out6);
  or or_3 (LD, AND_3_out, ADD_out, LD_out, OR_2_out, XOR_out, and_4_out, XCHG_out, INC_out, CME_out, SHR_out, SHL_out);
  Priority_Encoder priority_encoder_1 (
    .in0(AND_3_out), .in1(ADD_out), .in2(LD_out), .in3(OR_2_out), .in4(XOR_out), .in5(CME_out),
    .in6(SHR_out), .in7(SHL_out), .out(ALUout));  // open: en_in, gs, en_out
endmodule

module SC_Controller (
  input  [21:0] IR,
  input  [15:0] Seq,
  input  R,
  output CLR
);

  wire and_3_out, and_4_out, and_5_out, and_6_out, and_7_out, and_8_out, and_9_out, and_10_out, and_11_out,
       and_12_out, and_13_out, decoder_2_out0, decoder_2_out1, decoder_2_out2, decoder_2_out3,
       decoder_2_out4, decoder_2_out5, decoder_2_out6, decoder_2_out7, decoder_2_out8, decoder_2_out9,
       decoder_2_out10, decoder_2_out11, decoder_2_out12, decoder_2_out13, decoder_2_out14, decoder_2_out15,
       I0, I1, I2, I3, m, p, r_t;

  and and_1 (r_t, I2, Seq[3]);
  and and_2 (p, I3, Seq[3]);
  Decoder #(.select(2)) decoder_1 (.out0(I0), .out1(I1), .out2(I2), .out3(I3), .sel(IR[21:20]));  // open: en
  or or_1 (m, I0, I1);
  Decoder #(.select(4)) decoder_2 (
    .out0(decoder_2_out0), .out1(decoder_2_out1), .out2(decoder_2_out2), .out3(decoder_2_out3),
    .out4(decoder_2_out4), .out5(decoder_2_out5), .out6(decoder_2_out6), .out7(decoder_2_out7),
    .out8(decoder_2_out8), .out9(decoder_2_out9), .out10(decoder_2_out10), .out11(decoder_2_out11),
    .out12(decoder_2_out12), .out13(decoder_2_out13), .out14(decoder_2_out14), .out15(decoder_2_out15),
    .sel(IR[19:16]));  // open: en
  and and_3 (and_3_out, m, decoder_2_out0, Seq[8]);
  and and_4 (and_4_out, m, decoder_2_out1, Seq[8]);
  and and_5 (and_5_out, m, decoder_2_out2, Seq[8]);
  and and_6 (and_6_out, m, decoder_2_out3, Seq[4]);
  and and_7 (and_7_out, m, decoder_2_out4, Seq[4]);
  and and_8 (and_8_out, m, decoder_2_out5, Seq[8]);
  and and_9 (and_9_out, m, decoder_2_out6, Seq[6]);
  and and_10 (and_10_out, m, decoder_2_out7, Seq[8]);
  and and_11 (and_11_out, m, decoder_2_out8, Seq[8]);
  and and_12 (and_12_out, m, decoder_2_out9, Seq[8]);
  and and_13 (and_13_out, R, Seq[2]);
  or or_2 (CLR, and_3_out, and_4_out, and_5_out, and_6_out, and_7_out, and_8_out, and_9_out, and_10_out, and_11_out, and_12_out, and_13_out, r_t, p);

  assign {Seq[7], Seq[5]} = {2{Seq[8]}};
endmodule

module SC (
  input  CLK,
  input  CLR,
  output [3:0] Tout
);

  wire controlled_buffer_1_out;
  wire [3:0] adder_1_out;

  Adder #(.width(4)) adder_1 (.a(Tout), .b(4'b0001), .out(adder_1_out));  // open: cin, cout
  assign controlled_buffer_1_out = CLK ? CLR : 1'bz;  // Controlled_Buffer controlled_buffer_1
  Register #(.width(4), .trigger("falling")) register_1 (
    .D(adder_1_out), .Q(Tout), .clk(CLK), .clr(controlled_buffer_1_out));  // open: en
endmodule

module TR_Controller (
  input  [21:0] IR,
  input  [15:0] Seq,
  input  R,
  output LD
);

  wire decoder_2_out0, decoder_2_out1, decoder_2_out2, decoder_2_out3, decoder_2_out4, decoder_2_out5,
       decoder_2_out6, decoder_2_out7, decoder_2_out8, decoder_2_out9, decoder_2_out10, decoder_2_out11,
       decoder_2_out12, decoder_2_out13, decoder_2_out14, decoder_2_out15, I0, I1, I2, I3, m, p, r_t;

  and and_1 (r_t, I2, Seq[3]);
  and and_2 (p, I3, Seq[3]);
  Decoder #(.select(2)) decoder_1 (.out0(I0), .out1(I1), .out2(I2), .out3(I3), .sel(IR[21:20]));  // open: en
  or or_1 (m, I0, I1);
  Decoder #(.select(4)) decoder_2 (
    .out0(decoder_2_out0), .out1(decoder_2_out1), .out2(decoder_2_out2), .out3(decoder_2_out3),
    .out4(decoder_2_out4), .out5(decoder_2_out5), .out6(decoder_2_out6), .out7(decoder_2_out7),
    .out8(decoder_2_out8), .out9(decoder_2_out9), .out10(decoder_2_out10), .out11(decoder_2_out11),
    .out12(decoder_2_out12), .out13(decoder_2_out13), .out14(decoder_2_out14), .out15(decoder_2_out15),
    .sel(IR[19:16]));  // open: en
  and and_3 (LD, R, Seq[0]);
endmodule

module IR (
  input  [21:0] in,
  input  LD,
  input  CLK,
  output [21:0] out
);

  Register #(.width(22)) register_1 (.D(in), .en(LD), .Q(out), .clk(CLK));  // open: clr
endmodule

module IR_Controller (
  input  [3:0] T,
  input  R,
  output LD
);

  wire decoder_1_out1;

  Decoder #(.select(4)) decoder_1 (
    .out1(decoder_1_out1), .sel(T));  // open: out0, out2, out3, out4, out5, out6, out7, out8, out9, out10, out11, out12, out13, out14, out15, en
  and and_1 (LD, ~R, decoder_1_out1);  // AND_Gate
endmodule

module TR (
  input  [21:0] in,
  input  LD,
  input  INC,
  input  CLR,
  input  CLK,
  output [21:0] out
);

  wire or_1_out;
  wire [21:0] adder_1_out, multiplexer_1_out;

  Adder #(.width(22)) adder_1 (.a(out), .b(22'h1), .out(adder_1_out));  // open: cin, cout
  or or_1 (or_1_out, LD, INC);
  Multiplexer #(.width(22)) multiplexer_1 (
    .in0(in), .in1(adder_1_out), .out(multiplexer_1_out), .sel(INC));  // open: en
  Register #(.width(22)) register_1 (.D(multiplexer_1_out), .en(or_1_out), .Q(out), .clk(CLK), .clr(CLR));
endmodule

module OUTR_Controller (
  input  [21:0] IR,
  input  [15:0] Seq,
  output LD
);

  wire decoder_2_out0, decoder_2_out1, decoder_2_out2, decoder_2_out3, decoder_2_out4, decoder_2_out5,
       decoder_2_out6, decoder_2_out7, decoder_2_out8, decoder_2_out9, decoder_2_out10, decoder_2_out11,
       decoder_2_out12, decoder_2_out13, decoder_2_out14, decoder_2_out15, I0, I1, I2, I3, m, p, r;

  and and_1 (r, I2, Seq[3]);
  and and_2 (p, I3, Seq[3]);
  Decoder #(.select(2)) decoder_1 (.out0(I0), .out1(I1), .out2(I2), .out3(I3), .sel(IR[21:20]));  // open: en
  or or_1 (m, I0, I1);
  Decoder #(.select(4)) decoder_2 (
    .out0(decoder_2_out0), .out1(decoder_2_out1), .out2(decoder_2_out2), .out3(decoder_2_out3),
    .out4(decoder_2_out4), .out5(decoder_2_out5), .out6(decoder_2_out6), .out7(decoder_2_out7),
    .out8(decoder_2_out8), .out9(decoder_2_out9), .out10(decoder_2_out10), .out11(decoder_2_out11),
    .out12(decoder_2_out12), .out13(decoder_2_out13), .out14(decoder_2_out14), .out15(decoder_2_out15),
    .sel(IR[19:16]));  // open: en
  and and_3 (LD, p, decoder_2_out1);
endmodule

module Memory_Write (
  input  [21:0] IR,
  input  [15:0] Seq,
  input  R
);

  wire decoder_2_out0, decoder_2_out1, decoder_2_out2, decoder_2_out3, decoder_2_out4, decoder_2_out5,
       decoder_2_out6, decoder_2_out7, decoder_2_out8, decoder_2_out9, decoder_2_out10, decoder_2_out11,
       decoder_2_out12, decoder_2_out13, decoder_2_out14, decoder_2_out15, I0, I1, I2, I3, m;

  Decoder #(.select(2)) decoder_1 (.out0(I0), .out1(I1), .out2(I2), .out3(I3), .sel(IR[21:20]));  // open: en
  or or_1 (m, I0, I1);
  Decoder #(.select(4)) decoder_2 (
    .out0(decoder_2_out0), .out1(decoder_2_out1), .out2(decoder_2_out2), .out3(decoder_2_out3),
    .out4(decoder_2_out4), .out5(decoder_2_out5), .out6(decoder_2_out6), .out7(decoder_2_out7),
    .out8(decoder_2_out8), .out9(decoder_2_out9), .out10(decoder_2_out10), .out11(decoder_2_out11),
    .out12(decoder_2_out12), .out13(decoder_2_out13), .out14(decoder_2_out14), .out15(decoder_2_out15),
    .sel(IR[19:16]));  // open: en
  // AND_Gate and_1 has open pins: in0=m, in1=decoder_2_out3, in2=Seq[4], out=open
  // AND_Gate and_2 has open pins: in0=m, in1=decoder_2_out6, in2=Seq[6], out=open
  // AND_Gate and_3 has open pins: in0=m, in1=decoder_2_out9, in2=Seq[5], out=open
  // AND_Gate and_4 has open pins: in0=R, in1=Seq[1], out=open
endmodule

module PC (
  input  [21:0] in,
  input  LD,
  input  INC,
  input  CLK,
  output [21:0] out
);

  wire or_1_out;
  wire [15:0] adder_1_out, multiplexer_1_out;

  Adder #(.width(16)) adder_1 (.a(out[15:0]), .b(16'h1), .out(adder_1_out));  // open: cin, cout
  or or_1 (or_1_out, LD, INC);
  Multiplexer #(.width(16)) multiplexer_1 (
    .in0(in[15:0]), .in1(adder_1_out), .out(multiplexer_1_out), .sel(INC));  // open: en
  Register #(.width(16)) register_1 (.D(multiplexer_1_out), .en(or_1_out), .Q(out[15:0]), .clk(CLK));  // open: clr
endmodule

module E_Control (
  input  [21:0] IR,
  input  [15:0] Seq,
  output LD,
  output CLR,
  output comp
);

  wire and_2_out, and_3_out, and_4_out, decoder_2_out0, decoder_2_out1, decoder_2_out2, decoder_2_out3,
       decoder_2_out4, decoder_2_out5, decoder_2_out6, decoder_2_out7, decoder_2_out8, decoder_2_out9,
       decoder_2_out10, decoder_2_out11, decoder_2_out12, decoder_2_out13, decoder_2_out14, decoder_2_out15,
       I0, I1, I2, I3, m, r;

  and and_1 (r, I2, Seq[3]);
  Decoder #(.select(2)) decoder_1 (.out0(I0), .out1(I1), .out2(I2), .out3(I3), .sel(IR[21:20]));  // open: en
  or or_1 (m, I0, I1);
  Decoder #(.select(4)) decoder_2 (
    .out0(decoder_2_out0), .out1(decoder_2_out1), .out2(decoder_2_out2), .out3(decoder_2_out3),
    .out4(decoder_2_out4), .out5(decoder_2_out5), .out6(decoder_2_out6), .out7(decoder_2_out7),
    .out8(decoder_2_out8), .out9(decoder_2_out9), .out10(decoder_2_out10), .out11(decoder_2_out11),
    .out12(decoder_2_out12), .out13(decoder_2_out13), .out14(decoder_2_out14), .out15(decoder_2_out15),
    .sel(IR[19:16]));  // open: en
  and and_2 (and_2_out, m, decoder_2_out1, Seq[5]);
  and and_3 (and_3_out, r, decoder_2_out4);
  and and_4 (and_4_out, r, decoder_2_out5);
  or or_2 (LD, and_2_out, and_3_out, and_4_out);
  and and_5 (CLR, r, decoder_2_out1);
  and and_6 (comp, r, decoder_2_out2);
endmodule

module E (
  input  in,
  input  Comp,
  input  CLK,
  input  LD,
  input  CLR,
  output out
);

  wire j_k_ff_1_qn, multiplexer_1_out, not_1_out, or_1_out;

  Multiplexer multiplexer_1 (.in0(in), .in1(j_k_ff_1_qn), .out(multiplexer_1_out), .sel(Comp));  // open: en
  not not_1 (not_1_out, multiplexer_1_out);
  or or_1 (or_1_out, Comp, LD);
  J_K_Flip_Flop j_k_ff_1 (
    .J(multiplexer_1_out), .clk(CLK), .K(not_1_out), .Q(out), .Qn(j_k_ff_1_qn), .en(or_1_out), .reset(CLR));  // open: preset
endmodule

module Bus_Control (
  input  [3:0] SC,
  input  R,
  input  [21:0] IR,
  output [2:0] Bus_Select,
  output Read
);

  wire AC_out, and_3_out, and_4_out, and_5_out, and_6_out, and_7_out, and_8_out, and_9_out, and_10_out,
       and_11_out, and_12_out, and_13_out, and_14_out, and_15_out, and_16_out, and_17_out, and_18_out,
       and_19_out, and_20_out, and_21_out, and_22_out, and_23_out, and_24_out, and_25_out, AR_out,
       decoder_2_out0, decoder_2_out1, decoder_2_out2, decoder_2_out3, decoder_2_out4, decoder_2_out5,
       decoder_2_out6, decoder_2_out7, decoder_2_out8, decoder_3_out0, decoder_3_out1, decoder_3_out2,
       decoder_3_out3, decoder_3_out4, decoder_3_out5, decoder_3_out6, DR_out, I0, I1, I2, I3, IR_out, m, p,
       PC_out, r_t, TR_out;

  Decoder #(.select(2)) decoder_1 (.out0(I0), .out1(I1), .out2(I2), .out3(I3), .sel(IR[21:20]));  // open: en
  and and_1 (r_t, I2, decoder_3_out3);
  and and_2 (p, I3, decoder_3_out3);
  or or_1 (m, I0, I1);
  Decoder #(.select(4)) decoder_2 (
    .out0(decoder_2_out0), .out1(decoder_2_out1), .out2(decoder_2_out2), .out3(decoder_2_out3),
    .out4(decoder_2_out4), .out5(decoder_2_out5), .out6(decoder_2_out6), .out7(decoder_2_out7),
    .out8(decoder_2_out8), .out9(m), .sel(IR[19:16]));  // open: out10, out11, out12, out13, out14, out15, en
  Decoder #(.select(4)) decoder_3 (
    .out0(decoder_3_out0), .out1(decoder_3_out1), .out2(decoder_3_out2), .out3(decoder_3_out3),
    .out4(decoder_3_out4), .out5(decoder_3_out5), .out6(decoder_3_out6), .sel(SC));  // open: out7, out8, out9, out10, out11, out12, out13, out14, out15, en
  and and_3 (and_3_out, m, decoder_3_out4, decoder_2_out4);
  and and_4 (and_4_out, m, decoder_3_out5, decoder_2_out5);
  and and_5 (and_5_out, m, decoder_3_out4, decoder_2_out5);
  and and_6 (and_6_out, ~R, decoder_3_out0);  // AND_Gate
  and and_7 (and_7_out, R, decoder_3_out0);
  and and_8 (and_8_out, m, decoder_3_out5, decoder_2_out2);
  and and_9 (and_9_out, m, decoder_3_out6, decoder_2_out6);
  and and_10 (and_10_out, m, decoder_3_out5, m);
  and and_11 (and_11_out, m, decoder_3_out4, decoder_2_out3);
  and and_12 (and_12_out, m, decoder_3_out5, m);
  and and_13 (and_13_out, r_t, decoder_2_out4);
  and and_14 (and_14_out, r_t, decoder_2_out5);
  and and_15 (and_15_out, p, decoder_2_out1);
  and u_IR (IR_out, ~R, decoder_3_out2);  // AND_Gate
  and TR (TR_out, R, decoder_3_out1);
  and and_16 (and_16_out, ~R, decoder_3_out1);  // AND_Gate
  and and_17 (and_17_out, decoder_3_out3, I1);
  and and_18 (and_18_out, decoder_3_out4, m, decoder_2_out0);
  and and_19 (and_19_out, decoder_3_out4, m, decoder_2_out1);
  and and_20 (and_20_out, decoder_3_out4, m, decoder_2_out2);
  and and_21 (and_21_out, decoder_3_out4, m, decoder_2_out6);
  and and_22 (and_22_out, decoder_3_out4, m, decoder_2_out7);
  and and_23 (and_23_out, decoder_3_out4, m, decoder_2_out8);
  and and_24 (and_24_out, decoder_3_out4, m, m);
  or AR (AR_out, and_3_out, and_4_out);
  or PC (PC_out, and_5_out, and_6_out, and_7_out);
  or DR (DR_out, and_8_out, and_9_out, and_10_out);
  or AC (AC_out, and_11_out, and_12_out, and_13_out, and_14_out, and_15_out);
  or mem (Read, and_16_out, and_17_out, and_18_out, and_19_out, and_20_out, and_21_out, and_22_out, and_23_out, and_24_out);
  and and_25 (and_25_out, ~Read, ~TR_out, ~IR_out, ~AC_out, ~DR_out, ~PC_out, ~AR_out);  // AND_Gate
  Priority_Encoder priority_encoder_1 (
    .in0(and_25_out), .in1(AR_out), .in2(PC_out), .in3(DR_out), .in4(AC_out), .in5(IR_out), .in6(TR_out),
    .in7(Read), .out(Bus_Select));  // open: en_in, gs, en_out
endmodule

module IEN_Control (
  input  [21:0] IR,
  input  [15:0] Seq,
  input  R,
  output IENk,
  output IENj
);

  wire and_2_out, and_3_out, and_4_out, decoder_2_out0, decoder_2_out1, decoder_2_out2, decoder_2_out3,
       decoder_2_out4, decoder_2_out5, decoder_2_out6, decoder_2_out7, decoder_2_out8, decoder_2_out9,
       decoder_2_out10, decoder_2_out11, decoder_2_out12, decoder_2_out13, decoder_2_out14, decoder_2_out15,
       I0, I1, I2, I3, m, p;

  and and_1 (p, I3, Seq[3]);
  Decoder #(.select(2)) decoder_1 (.out0(I0), .out1(I1), .out2(I2), .out3(I3), .sel(IR[21:20]));  // open: en
  or or_1 (m, I0, I1);
  Decoder #(.select(4)) decoder_2 (
    .out0(decoder_2_out0), .out1(decoder_2_out1), .out2(decoder_2_out2), .out3(decoder_2_out3),
    .out4(decoder_2_out4), .out5(decoder_2_out5), .out6(decoder_2_out6), .out7(decoder_2_out7),
    .out8(decoder_2_out8), .out9(decoder_2_out9), .out10(decoder_2_out10), .out11(decoder_2_out11),
    .out12(decoder_2_out12), .out13(decoder_2_out13), .out14(decoder_2_out14), .out15(decoder_2_out15),
    .sel(IR[19:16]));  // open: en
  and and_2 (and_2_out, R, Seq[2]);
  and and_3 (and_3_out, p, decoder_2_out5);
  and and_4 (and_4_out, p, decoder_2_out4);
  or or_2 (IENk, and_2_out, and_3_out);
endmodule

module R_Control (
  input  [3:0] T,
  input  IEN,
  input  FGO,
  input  FGI,
  input  R,
  output Rj,
  output Rk
);

  wire decoder_1_out0, decoder_1_out1, decoder_1_out2, or_1_out;

  Decoder #(.select(4)) decoder_1 (
    .out0(decoder_1_out0), .out1(decoder_1_out1), .out2(decoder_1_out2), .sel(T));  // open: out3, out4, out5, out6, out7, out8, out9, out10, out11, out12, out13, out14, out15, en
  or or_1 (or_1_out, FGO, FGI);
  and and_1 (Rj, ~decoder_1_out0, ~decoder_1_out1, ~decoder_1_out2, IEN, or_1_out);  // AND_Gate
  and and_2 (Rk, decoder_1_out2, R);
endmodule

module ALU (
  input  [21:0] in,
  input  [21:0] DR,
  input  [2:0] Select,
  output [21:0] out,
  output Cout
);

  wire [21:0] adder_1_out, and_1_out, not_1_out, or_1_out, shifter_1_out, shifter_2_out, xor_1_out;

  assign and_1_out = in & DR;  // AND_Gate and_1, 22 bits wide
  assign or_1_out = in | DR;  // OR_Gate or_1, 22 bits wide
  assign xor_1_out = in ^ DR;  // XOR_Gate xor_1, 22 bits wide
  assign not_1_out = ~in;  // NOT_Gate not_1, 22 bits wide
  Adder #(.width(22)) adder_1 (.a(in), .b(DR), .out(adder_1_out), .cout(Cout));  // open: cin
  Shifter #(.width(22)) shifter_1 (.in(in), .\dist (5'b00001), .out(shifter_1_out));
  Shifter #(.width(22), .shift("lr")) shifter_2 (.in(in), .\dist (5'b00001), .out(shifter_2_out));
  Multiplexer #(.select(3), .width(22)) multiplexer_1 (
    .in0(and_1_out), .in1(adder_1_out), .in2(DR), .in3(or_1_out), .in4(xor_1_out), .in5(not_1_out),
    .in6(shifter_1_out), .in7(shifter_2_out), .out(out), .sel(Select));  // open: en
endmodule

module FGI_FGO_S (
  input  [7:0] OUTR,
  input  [21:0] IR,
  input  [15:0] Seq,
  input  [7:0] INPR,
  output Sk,
  output FGIk,
  output FGOk,
  output FGIj,
  output FGOj
);

  wire decoder_2_out0, decoder_2_out1, decoder_2_out2, decoder_2_out3, decoder_2_out4, decoder_2_out5,
       decoder_2_out6, decoder_2_out7, decoder_2_out8, decoder_2_out9, decoder_2_out10, decoder_2_out11,
       decoder_2_out12, decoder_2_out13, decoder_2_out14, decoder_2_out15, I0, I1, I2, I3, m, p, r;

  and and_1 (r, I2, Seq[3]);
  and and_2 (p, I3, Seq[3]);
  Decoder #(.select(2)) decoder_1 (.out0(I0), .out1(I1), .out2(I2), .out3(I3), .sel(IR[21:20]));  // open: en
  or or_1 (m, I0, I1);
  Decoder #(.select(4)) decoder_2 (
    .out0(decoder_2_out0), .out1(decoder_2_out1), .out2(decoder_2_out2), .out3(decoder_2_out3),
    .out4(decoder_2_out4), .out5(decoder_2_out5), .out6(decoder_2_out6), .out7(decoder_2_out7),
    .out8(decoder_2_out8), .out9(decoder_2_out9), .out10(decoder_2_out10), .out11(decoder_2_out11),
    .out12(decoder_2_out12), .out13(decoder_2_out13), .out14(decoder_2_out14), .out15(decoder_2_out15),
    .sel(IR[19:16]));  // open: en
  or or_2 (FGIj, INPR[7], INPR[6], INPR[5], INPR[4], INPR[2], INPR[1], INPR[0], INPR[3]);
  or or_3 (FGOj, OUTR[7], OUTR[6], OUTR[5], OUTR[4], OUTR[2], OUTR[1], OUTR[0], OUTR[3]);
  and and_3 (Sk, r, decoder_2_out11);
  and and_4 (FGIk, p, decoder_2_out11);
  and and_5 (FGOk, p, decoder_2_out1);
endmodule
